// Logisim project single_cycle_processor.circ as structural Verilog: 17 circuits, main circuit main
module main (
  output [31:0] out_1
);

  wire alu_1_zero, clock_1_out, control_unit_1_alusrc, control_unit_1_memwrite, control_unit_1_regwrite,
       instruction_decoder_1_funct7_3;
  wire [1:0] alu_1_result, control_unit_1_immsrc, control_unit_1_pcsrc, control_unit_1_resultsrc;
  wire [2:0] control_unit_1_alucontrol, instruction_decoder_1_funct3;
  wire [4:0] instruction_decoder_1_a1, instruction_decoder_1_a2, instruction_decoder_1_a3;
  wire [5:0] alu_1_result_2;
  wire [6:0] instruction_decoder_1_op;
  wire [23:0] alu_1_result_3;
  wire [24:0] instruction_decoder_1_imm;
  wire [31:0] adder_1_out, adder_2_out, adder_3_out, data_memory_1_rd, imm_extend_1_immext,
       instruction_memory_1_rd, multiplexer_1_out, multiplexer_2_out, multiplexer_3_out, register_file_1_rd1,
       register_file_1_rd2;

  // Probe on adder_1_out
  Adder #(.width(32)) adder_1 (
    .a({alu_1_result_3, alu_1_result_2, alu_1_result}), .b(imm_extend_1_immext), .out(adder_1_out));  // open: cin, cout
  Multiplexer #(.select(2), .width(32), .enable("false")) multiplexer_1 (
    .in0(adder_2_out), .in1(adder_3_out), .in3(adder_1_out), .out(multiplexer_1_out),
    .sel(control_unit_1_pcsrc));  // open: in2
  register register_1 (.S(multiplexer_1_out), .CLK(clock_1_out), .Q(out_1));
  // Probe on out_1
  // Probe on out_1
  Adder #(.width(32)) adder_2 (.a(out_1), .b(32'h4), .out(adder_2_out));  // open: cin, cout
  Instruction_decoder instruction_decoder_1 (
    .in_1(instruction_memory_1_rd), .op(instruction_decoder_1_op), .funct3(instruction_decoder_1_funct3),
    .funct7_3(instruction_decoder_1_funct7_3), .A1(instruction_decoder_1_a1), .A2(instruction_decoder_1_a2),
    .A3(instruction_decoder_1_a3), .Imm(instruction_decoder_1_imm));
  Instruction_Memory instruction_memory_1 (.Adress(out_1[7:2]), .RD(instruction_memory_1_rd));
  Control_Unit control_unit_1 (
    .Zero(alu_1_zero), .op(instruction_decoder_1_op), .func3(instruction_decoder_1_funct3),
    .funt7_5(instruction_decoder_1_funct7_3), .PCSrc(control_unit_1_pcsrc),
    .ResultSrc(control_unit_1_resultsrc), .MemWrite(control_unit_1_memwrite), .ALUSrc(control_unit_1_alusrc),
    .ImmSrc(control_unit_1_immsrc), .RegWrite(control_unit_1_regwrite), .ALUControl(control_unit_1_alucontrol));
  Clock clock_1 (.out(clock_1_out));
  // Probe on register_file_1_rd1
  Register_File register_file_1 (
    .WD3(multiplexer_3_out), .WE3(control_unit_1_regwrite), .A3(instruction_decoder_1_a3),
    .A1(instruction_decoder_1_a1), .A2(instruction_decoder_1_a2), .RD1(register_file_1_rd1),
    .RD2(register_file_1_rd2), .in_1(clock_1_out));
  Imm_Extend imm_extend_1 (
    .ImmInput(instruction_decoder_1_imm), .ImmExt(imm_extend_1_immext), .ImmSrc(control_unit_1_immsrc));
  // Probe on imm_extend_1_immext
  Multiplexer #(.width(32), .enable("false")) multiplexer_2 (
    .in0(register_file_1_rd2), .in1(imm_extend_1_immext), .out(multiplexer_2_out), .sel(control_unit_1_alusrc));
  ALU alu_1 (
    .ALUControl(control_unit_1_alucontrol), .A(register_file_1_rd1), .B(multiplexer_2_out),
    .Zero(alu_1_zero), .Result({alu_1_result_3, alu_1_result_2, alu_1_result}));  // open: oVerflow, Carry, Negative
  Adder #(.width(32)) adder_3 (.a(out_1), .b(imm_extend_1_immext), .out(adder_3_out));  // open: cin, cout
  // Probe on {alu_1_result_3, alu_1_result_2, alu_1_result}
  // Probe on adder_2_out
  Data_Memory data_memory_1 (
    .A(alu_1_result_2), .WD(register_file_1_rd2), .RD(data_memory_1_rd), .WE(control_unit_1_memwrite),
    .CLK(clock_1_out));
  // Probe on control_unit_1_resultsrc
  Multiplexer #(.select(2), .width(32), .enable("false")) multiplexer_3 (
    .in0({alu_1_result_3, alu_1_result_2, alu_1_result}), .in1(data_memory_1_rd), .in2(adder_2_out),
    .out(multiplexer_3_out), .sel(control_unit_1_resultsrc));  // open: in3
  // Probe on multiplexer_3_out
endmodule

module Instruction_Memory (
  input  [5:0] Adress,
  output [31:0] RD
);

  ROM #(.addrWidth(6), .dataWidth(32)) rom_1 (.addr(Adress), .data(RD));  // open: sel

  // Notes on the sheet:
  //   contents of rom_1 (hex, n*v repeats v):
  //   0 0 8000113 2300413 2900493 40533 485b3 c000ef 950433 340006f ff810113 112223 a12023 b50533 18000ef
  //   12283 40a28533 412083 810113 8067 fe050513 8067 40433 ffdff06f
endmodule

module Register_File (
  input  in_1,
  input  [31:0] WD3,
  input  WE3,
  input  [4:0] A3,
  input  [4:0] A1,
  input  [4:0] A2,
  output [31:0] RD1,
  output [31:0] RD2
);

  wire demultiplexer_1_out0, demultiplexer_1_out1, demultiplexer_1_out2, demultiplexer_1_out3,
       demultiplexer_1_out4, demultiplexer_1_out5, demultiplexer_1_out6, demultiplexer_1_out7,
       demultiplexer_1_out8, demultiplexer_1_out9, demultiplexer_1_out10, demultiplexer_1_out11,
       demultiplexer_1_out12, demultiplexer_1_out13, demultiplexer_1_out14, demultiplexer_1_out15,
       demultiplexer_1_out16, demultiplexer_1_out17, demultiplexer_1_out18, demultiplexer_1_out19,
       demultiplexer_1_out20, demultiplexer_1_out21, demultiplexer_1_out22, demultiplexer_1_out23,
       demultiplexer_1_out24, demultiplexer_1_out25, demultiplexer_1_out26, demultiplexer_1_out27,
       demultiplexer_1_out28, demultiplexer_1_out29, demultiplexer_1_out30, demultiplexer_1_out31;
  wire [31:0] register_1_q, register_2_q, register_3_q, register_4_q, register_5_q, register_6_q,
       register_7_q, register_8_q, register_9_q, register_10_q, register_11_q, register_12_q, register_13_q,
       register_14_q, register_15_q, register_16_q, register_17_q, register_18_q, register_19_q,
       register_20_q, register_21_q, register_22_q, register_23_q, register_24_q, register_25_q,
       register_26_q, register_27_q, register_28_q, register_29_q, register_30_q, register_31_q,
       register_32_q;

  // Probe on WD3
  Demultiplexer #(.select(5)) demultiplexer_1 (
    .out0(demultiplexer_1_out0), .out1(demultiplexer_1_out1), .out2(demultiplexer_1_out2),
    .out3(demultiplexer_1_out3), .out4(demultiplexer_1_out4), .out5(demultiplexer_1_out5),
    .out6(demultiplexer_1_out6), .out7(demultiplexer_1_out7), .out8(demultiplexer_1_out8),
    .out9(demultiplexer_1_out9), .out10(demultiplexer_1_out10), .out11(demultiplexer_1_out11),
    .out12(demultiplexer_1_out12), .out13(demultiplexer_1_out13), .out14(demultiplexer_1_out14),
    .out15(demultiplexer_1_out15), .out16(demultiplexer_1_out16), .out17(demultiplexer_1_out17),
    .out18(demultiplexer_1_out18), .out19(demultiplexer_1_out19), .out20(demultiplexer_1_out20),
    .out21(demultiplexer_1_out21), .out22(demultiplexer_1_out22), .out23(demultiplexer_1_out23),
    .out24(demultiplexer_1_out24), .out25(demultiplexer_1_out25), .out26(demultiplexer_1_out26),
    .out27(demultiplexer_1_out27), .out28(demultiplexer_1_out28), .out29(demultiplexer_1_out29),
    .out30(demultiplexer_1_out30), .out31(demultiplexer_1_out31), .in(WE3), .sel(A3));  // open: en
  // NOT_Gate not_1 has open pins: in=WE3, out=open
  Register #(.width(32)) register_1 (
    .D({32{1'b0}}), .en(demultiplexer_1_out0), .Q(register_1_q), .clk(in_1));  // open: clr
  // Probe on register_1_q
  Register #(.width(32)) register_2 (.D(WD3), .en(demultiplexer_1_out1), .Q(register_2_q), .clk(in_1));  // open: clr
  // Probe on register_2_q
  Register #(.width(32)) register_3 (.D(WD3), .en(demultiplexer_1_out2), .Q(register_3_q), .clk(in_1));  // open: clr
  // Probe on register_3_q
  Register #(.width(32)) register_4 (.D(WD3), .en(demultiplexer_1_out3), .Q(register_4_q), .clk(in_1));  // open: clr
  // Probe on register_4_q
  Register #(.width(32)) register_5 (.D(WD3), .en(demultiplexer_1_out4), .Q(register_5_q), .clk(in_1));  // open: clr
  // Probe on register_5_q
  Register #(.width(32)) register_6 (.D(WD3), .en(demultiplexer_1_out5), .Q(register_6_q), .clk(in_1));  // open: clr
  // Probe on register_6_q
  Register #(.width(32)) register_7 (.D(WD3), .en(demultiplexer_1_out6), .Q(register_7_q), .clk(in_1));  // open: clr
  // Probe on register_7_q
  Register #(.width(32)) register_8 (.D(WD3), .en(demultiplexer_1_out7), .Q(register_8_q), .clk(in_1));  // open: clr
  // Probe on register_8_q
  Register #(.width(32)) register_9 (.D(WD3), .en(demultiplexer_1_out8), .Q(register_9_q), .clk(in_1));  // open: clr
  // Probe on register_9_q
  Register #(.width(32)) register_10 (.D(WD3), .en(demultiplexer_1_out9), .Q(register_10_q), .clk(in_1));  // open: clr
  // Probe on register_10_q
  Register #(.width(32)) register_11 (.D(WD3), .en(demultiplexer_1_out10), .Q(register_11_q), .clk(in_1));  // open: clr
  // Probe on register_11_q
  Register #(.width(32)) register_12 (.D(WD3), .en(demultiplexer_1_out11), .Q(register_12_q), .clk(in_1));  // open: clr
  // Probe on register_12_q
  Register #(.width(32)) register_13 (.D(WD3), .en(demultiplexer_1_out12), .Q(register_13_q), .clk(in_1));  // open: clr
  // Probe on register_13_q
  Register #(.width(32)) register_14 (.D(WD3), .en(demultiplexer_1_out13), .Q(register_14_q), .clk(in_1));  // open: clr
  // Probe on register_14_q
  Register #(.width(32)) register_15 (.D(WD3), .en(demultiplexer_1_out14), .Q(register_15_q), .clk(in_1));  // open: clr
  // Probe on register_15_q
  Register #(.width(32)) register_16 (.D(WD3), .en(demultiplexer_1_out15), .Q(register_16_q), .clk(in_1));  // open: clr
  // Probe on register_16_q
  Register #(.width(32)) register_17 (.D(WD3), .en(demultiplexer_1_out16), .Q(register_17_q), .clk(in_1));  // open: clr
  // Probe on register_17_q
  Register #(.width(32)) register_18 (.D(WD3), .en(demultiplexer_1_out17), .Q(register_18_q), .clk(in_1));  // open: clr
  Register #(.width(32)) register_19 (.D(WD3), .en(demultiplexer_1_out18), .Q(register_19_q), .clk(in_1));  // open: clr
  // Probe on register_19_q
  Register #(.width(32)) register_20 (.D(WD3), .en(demultiplexer_1_out19), .Q(register_20_q), .clk(in_1));  // open: clr
  // Probe on register_20_q
  Register #(.width(32)) register_21 (.D(WD3), .en(demultiplexer_1_out20), .Q(register_21_q), .clk(in_1));  // open: clr
  // Probe on register_21_q
  Register #(.width(32)) register_22 (.D(WD3), .en(demultiplexer_1_out21), .Q(register_22_q), .clk(in_1));  // open: clr
  // Probe on register_22_q
  Register #(.width(32)) register_23 (.D(WD3), .en(demultiplexer_1_out22), .Q(register_23_q), .clk(in_1));  // open: clr
  // Probe on register_23_q
  Register #(.width(32)) register_24 (.D(WD3), .en(demultiplexer_1_out23), .Q(register_24_q), .clk(in_1));  // open: clr
  // Probe on register_24_q
  Register #(.width(32)) register_25 (.D(WD3), .en(demultiplexer_1_out24), .Q(register_25_q), .clk(in_1));  // open: clr
  // Probe on register_25_q
  Register #(.width(32)) register_26 (.D(WD3), .en(demultiplexer_1_out25), .Q(register_26_q), .clk(in_1));  // open: clr
  // Probe on register_26_q
  Register #(.width(32)) register_27 (.D(WD3), .en(demultiplexer_1_out26), .Q(register_27_q), .clk(in_1));  // open: clr
  // Probe on register_27_q
  Register #(.width(32)) register_28 (.D(WD3), .en(demultiplexer_1_out27), .Q(register_28_q), .clk(in_1));  // open: clr
  // Probe on register_28_q
  Register #(.width(32)) register_29 (.D(WD3), .en(demultiplexer_1_out28), .Q(register_29_q), .clk(in_1));  // open: clr
  // Probe on register_29_q
  Register #(.width(32)) register_30 (.D(WD3), .en(demultiplexer_1_out29), .Q(register_30_q), .clk(in_1));  // open: clr
  // Probe on register_30_q
  Register #(.width(32)) register_31 (.D(WD3), .en(demultiplexer_1_out30), .Q(register_31_q), .clk(in_1));  // open: clr
  // Probe on register_31_q
  Register #(.width(32)) register_32 (.D(WD3), .en(demultiplexer_1_out31), .Q(register_32_q), .clk(in_1));  // open: clr
  // Probe on register_32_q
  Multiplexer #(.select(5), .width(32)) multiplexer_1 (
    .in0(register_1_q), .in1(register_2_q), .in2(register_3_q), .in3(register_4_q), .in4(register_5_q),
    .in5(register_6_q), .in6(register_7_q), .in7(register_8_q), .in8(register_9_q), .in9(register_10_q),
    .in10(register_11_q), .in11(register_12_q), .in12(register_13_q), .in13(register_14_q),
    .in14(register_15_q), .in15(register_16_q), .in16(register_17_q), .in17(register_18_q),
    .in18(register_19_q), .in19(register_20_q), .in20(register_21_q), .in21(register_22_q),
    .in22(register_23_q), .in23(register_24_q), .in24(register_25_q), .in25(register_26_q),
    .in26(register_27_q), .in27(register_28_q), .in28(register_29_q), .in29(register_30_q),
    .in30(register_31_q), .in31(register_32_q), .out(RD1), .sel(A1));  // open: en
  Multiplexer #(.select(5), .width(32)) multiplexer_2 (
    .in0(register_1_q), .in1(register_2_q), .in2(register_3_q), .in3(register_4_q), .in4(register_5_q),
    .in5(register_6_q), .in6(register_7_q), .in7(register_8_q), .in8(register_9_q), .in9(register_10_q),
    .in10(register_11_q), .in11(register_12_q), .in12(register_13_q), .in13(register_14_q),
    .in14(register_15_q), .in15(register_16_q), .in16(register_17_q), .in17(register_18_q),
    .in18(register_19_q), .in19(register_20_q), .in20(register_21_q), .in21(register_22_q),
    .in22(register_23_q), .in23(register_24_q), .in24(register_25_q), .in25(register_26_q),
    .in26(register_27_q), .in27(register_28_q), .in28(register_29_q), .in29(register_30_q),
    .in30(register_31_q), .in31(register_32_q), .out(RD2), .sel(A2));  // open: en
endmodule

module Imm_Extend (
  input  [24:0] ImmInput,
  input  [1:0] ImmSrc,
  output [31:0] ImmExt
);

  wire [31:0] bit_extender_1_out, bit_extender_2_out, bit_extender_3_out, bit_extender_4_out;

  // Probe on ImmInput
  assign bit_extender_1_out = {{20{ImmInput[24]}}, {ImmInput[24:18], ImmInput[4:0]}};  // Bit_Extender bit_extender_1
  assign bit_extender_2_out = {{20{ImmInput[24]}}, ImmInput[24:13]};  // Bit_Extender bit_extender_2
  assign bit_extender_3_out = {{19{ImmInput[24]}}, {ImmInput[24], ImmInput[0], ImmInput[23:18], ImmInput[4:1], 1'b0}};  // Bit_Extender bit_extender_3
  assign bit_extender_4_out = {{11{ImmInput[24]}}, {ImmInput[24], ImmInput[12:5], ImmInput[13], ImmInput[23:14], 1'b0}};  // Bit_Extender bit_extender_4
  // Probe on bit_extender_4_out
  Multiplexer #(.select(2), .width(32), .enable("false")) multiplexer_1 (
    .in0(bit_extender_2_out), .in1(bit_extender_1_out), .in2(bit_extender_3_out), .in3(bit_extender_4_out),
    .out(ImmExt), .sel(ImmSrc));
endmodule

module ALU (
  input  [31:0] A,
  input  [31:0] B,
  input  [2:0] ALUControl,
  output [31:0] Result,
  output oVerflow,
  output Carry,
  output Negative,
  output Zero
);

  wire adder_1_cout, and_4_out, and_5_out, not_1_out, not_2_out, not_5_out, or_2_out, or_3_out, Sum31,
       xor_1_out, xor_2_out;
  wire [30:0] adder_1_out;
  wire [31:0] and_3_out, bit_extender_1_out, multiplexer_1_out, not_3_out, or_1_out;

  ExactlyOne xor_1 (.out(xor_1_out), .in0(ALUControl[0]), .in1(A[31]), .in2(B[31]));
  not not_1 (not_1_out, xor_1_out);
  xor xor_2 (xor_2_out, A[31], Sum31);
  and and_1 (oVerflow, not_1_out, xor_2_out, not_2_out);
  not not_2 (not_2_out, ALUControl[1]);
  and and_2 (Carry, not_2_out, adder_1_cout);
  assign and_3_out = A & B;  // AND_Gate and_3, 32 bits wide
  assign or_1_out = A | B;  // OR_Gate or_1, 32 bits wide
  assign not_3_out = ~B;  // NOT_Gate not_3, 32 bits wide
  Multiplexer #(.width(32), .enable("false")) multiplexer_1 (
    .in0(B), .in1(not_3_out), .out(multiplexer_1_out), .sel(ALUControl[0]));
  Adder #(.width(32)) adder_1 (
    .a(A), .b(multiplexer_1_out), .out({Sum31, adder_1_out}), .cin(ALUControl[0]), .cout(adder_1_cout));
  Multiplexer #(.select(3), .width(32), .enable("false")) multiplexer_2 (
    .in0({Sum31, adder_1_out}), .in1({Sum31, adder_1_out}), .in2(and_3_out), .in3(or_1_out),
    .in5(bit_extender_1_out), .out({Negative, Result[30:0]}), .sel(ALUControl));  // open: in4, in6, in7
  or or_2 (or_2_out, Negative, Result[30], Result[29], Result[28], Result[27], Result[26], Result[25], Result[24], Result[23], Result[22], Result[21], Result[20], Result[19], Result[18], Result[17], Result[16], Result[15], Result[14], Result[13], Result[12], Result[11], Result[10], Result[9], Result[8], Result[7], Result[6], Result[5], Result[4], Result[3], Result[2], Result[1], Result[0]);
  not not_4 (Zero, or_2_out);
  and and_4 (and_4_out, Sum31, not_5_out);
  not not_5 (not_5_out, oVerflow);
  and and_5 (and_5_out, A[31], oVerflow);
  or or_3 (or_3_out, and_4_out, and_5_out);
  assign bit_extender_1_out = {{31{1'b0}}, or_3_out};  // Bit_Extender bit_extender_1

  assign Result[31] = Negative;
endmodule

module Data_Memory (
  input  [5:0] A,
  input  [31:0] WD,
  input  WE,
  input  CLK,
  output [31:0] RD
);

  wire not_1_out;

  not not_1 (not_1_out, WE);
  RAM #(.addrWidth(6), .dataWidth(32), .bus("separate")) ram_1 (
    .addr(A), .din(WD), .data(RD), .str(WE), .clk(CLK), .ld(not_1_out));  // open: sel, clr
endmodule

module Control_Unit (
  input  Zero,
  input  [6:0] op,
  input  [2:0] func3,
  input  funt7_5,
  output [1:0] PCSrc,
  output [1:0] ResultSrc,
  output MemWrite,
  output ALUSrc,
  output [1:0] ImmSrc,
  output RegWrite,
  output [2:0] ALUControl
);

  wire and_1_out, branch_1_memwrite, jump_1_jump, not_1_out, not_2_out;
  wire [1:0] aluop_1_aluop;
  wire [2:0] multiplexer_1_out, multiplexer_2_out;

  Multiplexer #(.select(2), .width(3), .enable("false")) multiplexer_1 (
    .in0(3'b000), .in1(3'b000), .in2(3'b000), .in3(3'b001), .out(multiplexer_1_out), .sel({op[5], funt7_5}));
  Branch branch_1 (.MemWrite(branch_1_memwrite), .Opcode(op[6:2]));
  Jump jump_1 (.Jump(jump_1_jump), .Opcode(op[6:2]));
  ResultSrc resultsrc_1 (.ResultSrc(ResultSrc), .Opcode(op[6:2]));
  MemWrite memwrite_1 (.MemWrite(MemWrite), .Opcode(op[6:2]));
  ALUSrc alusrc_1 (.out_2(ALUSrc), .Opcode(op[6:2]));
  ImmSrc immsrc_1 (.Opcode(op[6:2]), .ImmSrc(ImmSrc));
  RegWrite regwrite_1 (.out_2(RegWrite), .Opcode(op[6:2]));
  ALUop aluop_1 (.ALUOp(aluop_1_aluop), .Opcode(op[6:2]));
  Multiplexer #(.select(3), .width(3), .enable("false")) multiplexer_2 (
    .in0(multiplexer_1_out), .in2(3'b101), .in6(3'b011), .in7(3'b010), .out(multiplexer_2_out), .sel(func3));  // open: in1, in3, in4, in5
  and and_1 (and_1_out, Zero, branch_1_memwrite);
  not not_1 (not_1_out, op[3]);
  not not_2 (not_2_out, op[4]);
  and and_2 (PCSrc[1], op[2], not_1_out, not_2_out, op[5], op[6]);
  or or_1 (PCSrc[0], and_1_out, jump_1_jump);
  Multiplexer #(.select(2), .width(3), .enable("false")) multiplexer_3 (
    .in0(3'b000), .in1(3'b001), .in2(multiplexer_2_out), .out(ALUControl), .sel(aluop_1_aluop));  // open: in3
endmodule

module RegWrite (
  input  [4:0] Opcode,
  output out_2
);

  wire and_1_out, and_2_out, and_3_out, not_1_out, not_2_out, not_3_out, not_4_out, not_5_out;

  not not_1 (not_1_out, Opcode[4]);
  not not_2 (not_2_out, Opcode[3]);
  not not_3 (not_3_out, Opcode[0]);
  not not_4 (not_4_out, Opcode[2]);
  not not_5 (not_5_out, Opcode[1]);
  and and_1 (and_1_out, Opcode[4], Opcode[3], not_4_out, Opcode[0]);
  and and_2 (and_2_out, not_1_out, Opcode[2], not_5_out, not_3_out);
  and and_3 (and_3_out, not_1_out, not_2_out, not_5_out, not_3_out);
  or or_1 (out_2, and_1_out, and_2_out, and_3_out);
endmodule

module ImmSrc (
  input  [4:0] Opcode,
  output [1:0] ImmSrc
);

  wire and_1_out, and_2_out, and_3_out, and_4_out, not_1_out, not_2_out, not_3_out, not_4_out, not_5_out;

  not not_1 (not_1_out, Opcode[3]);
  not not_2 (not_2_out, Opcode[4]);
  not not_3 (not_3_out, Opcode[2]);
  not not_4 (not_4_out, Opcode[0]);
  not not_5 (not_5_out, Opcode[1]);
  and and_1 (and_1_out, Opcode[4], Opcode[3], not_3_out, Opcode[1], Opcode[0]);
  and and_2 (and_2_out, Opcode[4], Opcode[3], not_3_out, not_5_out, not_4_out);
  and and_3 (and_3_out, Opcode[4], Opcode[3], not_3_out, Opcode[1], Opcode[0]);
  and and_4 (and_4_out, not_2_out, Opcode[3], not_3_out, not_5_out, not_4_out);
  or or_1 (ImmSrc[1], and_1_out, and_2_out);
  or or_2 (ImmSrc[0], and_3_out, and_4_out);
endmodule

module ALUSrc (
  input  [4:0] Opcode,
  output out_2
);

  wire and_1_out, and_2_out, and_3_out, not_1_out, not_2_out, not_3_out, not_4_out, not_5_out;

  not not_1 (not_1_out, Opcode[4]);
  not not_2 (not_2_out, Opcode[3]);
  not not_3 (not_3_out, Opcode[2]);
  not not_4 (not_4_out, Opcode[1]);
  not not_5 (not_5_out, Opcode[0]);
  and and_1 (and_1_out, Opcode[4], Opcode[3], not_3_out, not_4_out, Opcode[0]);
  and and_2 (and_2_out, not_1_out, not_2_out, not_4_out, not_5_out);
  and and_3 (and_3_out, not_1_out, not_3_out, not_4_out, not_5_out);
  or or_1 (out_2, and_1_out, and_2_out, and_3_out);
endmodule

module MemWrite (
  input  [4:0] Opcode,
  output MemWrite
);

  wire not_1_out, not_2_out, not_3_out, not_4_out, not_5_out;

  not not_1 (not_1_out, Opcode[3]);
  not not_2 (not_2_out, Opcode[4]);
  not not_3 (not_3_out, Opcode[2]);
  not not_4 (not_4_out, Opcode[1]);
  not not_5 (not_5_out, Opcode[0]);
  and and_1 (MemWrite, not_2_out, Opcode[3], not_3_out, not_4_out, not_5_out);
endmodule

module ResultSrc (
  input  [4:0] Opcode,
  output [1:0] ResultSrc
);

  wire not_1_out, not_2_out, not_3_out, not_4_out, not_5_out;

  not not_1 (not_1_out, Opcode[4]);
  not not_2 (not_2_out, Opcode[3]);
  not not_3 (not_3_out, Opcode[2]);
  not not_4 (not_4_out, Opcode[1]);
  not not_5 (not_5_out, Opcode[0]);
  and and_1 (ResultSrc[1], Opcode[4], Opcode[3], not_3_out, Opcode[0]);
  and and_2 (ResultSrc[0], not_1_out, not_2_out, not_3_out, not_4_out, not_5_out);
endmodule

module Branch (
  input  [4:0] Opcode,
  output MemWrite
);

  wire not_1_out, not_2_out, not_3_out, not_4_out, not_5_out;

  not not_1 (not_1_out, Opcode[3]);
  not not_2 (not_2_out, Opcode[4]);
  not not_3 (not_3_out, Opcode[2]);
  not not_4 (not_4_out, Opcode[0]);
  not not_5 (not_5_out, Opcode[1]);
  and and_1 (MemWrite, Opcode[4], Opcode[3], not_3_out, not_5_out, not_4_out);
endmodule

module ALUop (
  input  [4:0] Opcode,
  output [1:0] ALUOp
);

  wire and_1_out, and_2_out, not_1_out, not_2_out, not_3_out, not_4_out, not_5_out;

  not not_1 (not_1_out, Opcode[3]);
  not not_2 (not_2_out, Opcode[4]);
  not not_3 (not_3_out, Opcode[2]);
  not not_4 (not_4_out, Opcode[0]);
  not not_5 (not_5_out, Opcode[1]);
  and and_1 (and_1_out, not_2_out, Opcode[3], Opcode[2], not_5_out, not_4_out);
  and and_2 (and_2_out, not_2_out, not_1_out, Opcode[2], not_5_out, not_4_out);
  and and_3 (ALUOp[0], Opcode[4], Opcode[3], not_3_out, not_5_out, not_4_out);
  or or_1 (ALUOp[1], and_1_out, and_2_out);
endmodule

module Jump (
  input  [4:0] Opcode,
  output Jump
);

  wire not_1_out, not_2_out, not_3_out, not_4_out, not_5_out;

  not not_1 (not_1_out, Opcode[4]);
  not not_2 (not_2_out, Opcode[3]);
  not not_3 (not_3_out, Opcode[1]);
  not not_4 (not_4_out, Opcode[2]);
  not not_5 (not_5_out, Opcode[0]);
  and and_1 (Jump, Opcode[4], Opcode[3], not_4_out, Opcode[0]);
endmodule

module register (
  input  [31:0] S,
  input  CLK,
  output [31:0] Q
);

  Register #(.width(32)) register_1 (.D(S), .Q(Q), .clk(CLK));  // open: en, clr
endmodule

module Instruction_decoder (
  input  [31:0] in_1,
  output [6:0] op,
  output [2:0] funct3,
  output funct7_3,
  output [4:0] A1,
  output [4:0] A2,
  output [4:0] A3,
  output [24:0] Imm
);


  assign A1 = in_1[19:15];
  assign A2 = in_1[24:20];
  assign A3 = in_1[11:7];
  assign funct3 = in_1[14:12];
  assign funct7_3 = in_1[30];
  assign Imm = in_1[31:7];
  assign op = in_1[6:0];
endmodule
